// Logisim project CPU.circ as structural Verilog: 1 circuit, main circuit CPU
module CPU (
  output [15:0] out_1,
  output [15:0] out_2,
  output [15:0] out_3
);

  wire and_1_out, and_2_out, and_3_out, and_4_out, and_5_out, and_6_out, bitselector_1_out, clock_1_out,
       decoder_1_out0, decoder_1_out1, decoder_1_out2, decoder_1_out3, decoder_1_out4, decoder_1_out5,
       decoder_1_out6, not_1_out, not_2_out, or_1_out, or_2_out, or_3_out;
  wire [3:0] multiplexer_2_out;
  wire [6:0] bit_extender_2_out;
  wire [7:0] multiplexer_4_out;
  wire [15:0] alu_1_out, main_1_p7, main_1_p8, multiplexer_3_out, multiplexer_5_out, multiplexer_6_out,
       multiplexer_7_out, ram_1_data;
  wire [23:0] adder_1_out, bit_extender_1_out, multiplexer_1_out, register_1_q;
  wire [31:0] register_2_q, register_3_q;

  Multiplexer #(.width(24), .enable("false")) multiplexer_1 (
    .in0(adder_1_out), .in1({out_1[11:4], out_2}), .out(multiplexer_1_out), .sel(or_1_out));
  or or_1 (or_1_out, decoder_1_out3, and_1_out);
  assign bit_extender_1_out = {{23{1'b0}}, 1'b1};  // Bit_Extender bit_extender_1
  Register #(.width(24), .trigger("falling")) register_1 (
    .D(multiplexer_1_out), .Q(register_1_q), .clk(clock_1_out));  // open: en, clr
  and and_1 (and_1_out, decoder_1_out6, bitselector_1_out);
  Adder #(.width(24)) adder_1 (.a(register_1_q), .b(bit_extender_1_out), .out(adder_1_out));  // open: cin, cout
  BitSelector #(.width(16)) bitselector_1 (.in(main_1_p8), .out(bitselector_1_out), .sel(4'b0000));
  ROM #(.addrWidth(24), .dataWidth(32)) rom_1 (.addr(register_1_q), .data({out_2, out_1}));  // open: sel
  Decoder #(.select(4), .enable("false")) decoder_1 (
    .out0(decoder_1_out0), .out1(decoder_1_out1), .out2(decoder_1_out2), .out3(decoder_1_out3),
    .out4(decoder_1_out4), .out5(decoder_1_out5), .out6(decoder_1_out6), .sel(out_1[3:0]));  // open: out7, out8, out9, out10, out11, out12, out13, out14, out15
  Multiplexer #(.width(4), .enable("false")) multiplexer_2 (
    .in0(4'b0000), .in1(out_2[3:0]), .out(multiplexer_2_out), .sel(decoder_1_out1));
  and and_2 (and_2_out, decoder_1_out1, not_1_out);
  not not_1 (not_1_out, out_1[4]);
  or or_2 (or_2_out, and_2_out, decoder_1_out2, decoder_1_out0);
  not not_2 (not_2_out, out_1[5]);
  Clock clock_1 (.out(clock_1_out));
  ALU alu_1 (.A(out_3), .B(main_1_p8), .INSTR(out_1[7:4]), .Enable(decoder_1_out2), .OUT(alu_1_out));
  or or_3 (or_3_out, decoder_1_out2, decoder_1_out4, and_3_out);
  and and_3 (and_3_out, decoder_1_out1, not_2_out);
  and and_4 (and_4_out, decoder_1_out1, out_1[4]);
  and and_5 (and_5_out, out_1[5], decoder_1_out1);
  Multiplexer #(.width(16), .enable("false")) multiplexer_3 (
    .in0(out_3), .in1(alu_1_out), .out(multiplexer_3_out), .sel(decoder_1_out2));
  and and_6 (and_6_out, decoder_1_out1, out_1[5]);
  Multiplexer #(.width(8), .enable("false")) multiplexer_4 (
    .in0({8{1'b0}}), .in1(out_2[7:0]), .out(multiplexer_4_out), .sel(decoder_1_out1));
  Multiplexer #(.width(16), .enable("false")) multiplexer_5 (
    .in0({16{1'b0}}), .in1(main_1_p7), .out(multiplexer_5_out), .sel(or_3_out));
  Multiplexer #(.width(16), .enable("false")) multiplexer_6 (
    .in0({16{1'b0}}), .in1(ram_1_data), .out(multiplexer_6_out), .sel(and_6_out));
  // REGARRAY_main main_1: pin names not known; wires that end beside it: multiplexer_3_out, out_2[7:4], out_1[15:12], multiplexer_2_out, or_2_out, clock_1_out, main_1_p7, main_1_p8
  Multiplexer #(.width(16), .enable("false")) multiplexer_7 (
    .in0({16{1'b0}}), .in1(out_2), .out(multiplexer_7_out), .sel(decoder_1_out0));
  assign out_3 = multiplexer_7_out | multiplexer_5_out | multiplexer_6_out;  // OR_Gate or_4, 16 bits wide
  Register #(.width(32)) register_2 (.Q(register_2_q), .clk(clock_1_out));  // open: D, en, clr
  Register #(.width(32)) register_3 (.Q(register_3_q), .clk(clock_1_out));  // open: D, en, clr
  Bit_Extender #(.out_width(7)) bit_extender_2 (.in(out_3[7:0]), .out(bit_extender_2_out));
  DotMatrix #(.matrixcols(8), .matrixrows(8)) dotmatrix_1 (
    .col0(register_2_q[31:24]), .col1(register_2_q[23:16]), .col2(register_2_q[15:8]),
    .col3(register_2_q[7:0]), .col4(register_3_q[31:24]), .col5(register_3_q[23:16]),
    .col6(register_3_q[15:8]), .col7(register_3_q[7:0]));
  RAM #(.addrWidth(16), .dataWidth(16), .bus("separate")) ram_1 (
    .addr({out_1[15:8], multiplexer_4_out}), .din(out_3), .data(ram_1_data), .str(and_4_out), .sel(1'b1),
    .clk(clock_1_out), .ld(and_5_out));  // open: clr
  TTY #(.rows(32), .cols(100)) tty_1 (
    .data(bit_extender_2_out), .clk(clock_1_out), .we(decoder_1_out4), .clr(decoder_1_out5));

  // Notes on the sheet:
  //   0=immediate
  //   1=mov
  //   2=calc
  //   3=jmp
  //   4=wrt
  //   5=rssc
  //   6=JMI
  //   contents of rom_1 (hex, n*v repeats v):
  //   5 480000 4 450000 4 4c0000 4 4c0000 4 4f0000 4 200000 4 570000 4 4f0000 4 520000 4 4c0000 4 440000 4
  //   210000 4 3
  //   Write
  //   Read
endmodule
